// Logisim project A1.circ as structural Verilog: 1 circuit, main circuit main
module main (
  input  a,
  input  b,
  output z
);

  wire not_1_out, or_1_out;

  not not_1 (not_1_out, b);
  or or_1 (or_1_out, a, not_1_out);
  not not_2 (z, or_1_out);
endmodule
