// Logisim project A2.circ as structural Verilog: 1 circuit, main circuit main
module main (
  input  a,
  input  b,
  input  c,
  output z,
  output y
);

  wire and_1_out, and_2_out;

  and and_1 (and_1_out, a, b);
  and and_2 (and_2_out, b, c);
  and and_3 (z, and_1_out, c);
  and and_4 (y, a, and_2_out);
endmodule
