// Logisim project A3.circ as structural Verilog: 1 circuit, main circuit main
module main (
  input  a,
  input  b,
  input  c,
  output out_4
);

  wire or_1_out, or_2_out;

  or or_1 (or_1_out, a, c);
  or or_2 (or_2_out, a, b);
  and and_1 (out_4, or_1_out, or_2_out);
endmodule
