// Logisim project Lüfter.circ as structural Verilog: 1 circuit, main circuit main
module main (
  input  \lüfter1 ,
  input  \lüfter2 ,
  input  \lüfter1_2 ,
  input  \lüfter2_2 ,
  input  \lüfter1_3 ,
  input  \lüfter2_3 ,
  output meldung,
  output fehler,
  output meldung_2,
  output meldung_3,
  output fehler_2,
  output fehler_3,
  output meldung_4,
  output fehler_4
);

  wire and_1_out, and_2_out, and_4_out, and_5_out, and_7_out, and_8_out, not_1_out, not_2_out, not_3_out,
       not_4_out, not_5_out, not_6_out, not_7_out, not_8_out, not_9_out, not_10_out, not_11_out, not_12_out;

  not not_1 (not_1_out, \lüfter1 );
  not not_2 (not_2_out, \lüfter2 );
  not not_3 (not_3_out, \lüfter1 );
  not not_4 (not_4_out, \lüfter2 );
  not not_5 (not_5_out, \lüfter1_2 );
  not not_6 (not_6_out, \lüfter2_2 );
  not not_7 (not_7_out, \lüfter1_2 );
  not not_8 (not_8_out, \lüfter2_2 );
  not not_9 (not_9_out, \lüfter1_3 );
  not not_10 (not_10_out, \lüfter2_3 );
  not not_11 (not_11_out, \lüfter1_3 );
  not not_12 (not_12_out, \lüfter2_3 );
  and and_1 (and_1_out, not_1_out, \lüfter2 );
  and and_2 (and_2_out, \lüfter1 , not_2_out);
  and and_3 (fehler, not_3_out, not_4_out);
  and and_4 (and_4_out, not_5_out, \lüfter2_2 );
  and and_5 (and_5_out, \lüfter1_2 , not_6_out);
  and and_6 (fehler_2, not_7_out, not_8_out);
  and and_7 (and_7_out, not_9_out, \lüfter2_3 );
  and and_8 (and_8_out, \lüfter1_3 , not_10_out);
  and and_9 (fehler_4, not_11_out, not_12_out);
  or or_1 (meldung, and_1_out, and_2_out);
  or or_2 (meldung_3, and_4_out, and_5_out);
  or or_3 (meldung_4, and_7_out, and_8_out);
  or or_4 (meldung_2, meldung, meldung_3, meldung_4);
  or or_5 (fehler_3, fehler, fehler_4);
endmodule
