// Logisim project RAID.circ as structural Verilog: 1 circuit, main circuit main
module main (
  input  HDD1,
  input  HDD2,
  input  HDD3,
  input  HDD4,
  output Kentniss,
  output Dringend
);

  wire and_2_out, and_3_out, and_4_out, and_5_out, and_6_out, and_7_out, not_1_out, not_2_out, not_3_out,
       not_4_out, not_5_out, not_6_out, not_7_out, not_8_out, not_9_out, not_10_out, not_11_out, not_12_out;

  and and_1 (Kentniss, HDD1, HDD2, HDD3, HDD4);
  not not_1 (not_1_out, HDD1);
  and and_2 (and_2_out, not_1_out, not_2_out);
  not not_2 (not_2_out, HDD2);
  not not_3 (not_3_out, HDD1);
  and and_3 (and_3_out, not_3_out, not_4_out);
  not not_4 (not_4_out, HDD3);
  not not_5 (not_5_out, HDD1);
  and and_4 (and_4_out, not_5_out, not_6_out);
  not not_6 (not_6_out, HDD4);
  not not_7 (not_7_out, HDD2);
  and and_5 (and_5_out, not_7_out, not_8_out);
  not not_8 (not_8_out, HDD3);
  not not_9 (not_9_out, HDD2);
  and and_6 (and_6_out, not_9_out, not_10_out);
  not not_10 (not_10_out, HDD4);
  not not_11 (not_11_out, HDD3);
  and and_7 (and_7_out, not_11_out, not_12_out);
  not not_12 (not_12_out, HDD4);
  or or_1 (Dringend, and_2_out, and_3_out, and_4_out, and_5_out, and_6_out, and_7_out);
endmodule
