// Logisim project alarm.circ as structural Verilog: 1 circuit, main circuit main
module main (
  input  RFID,
  input  \tür_oben ,
  input  \tür_mitte ,
  input  \tür_unten ,
  output out_5
);

  wire not_1_out, or_1_out;

  or or_1 (or_1_out, \tür_oben , \tür_mitte , \tür_unten );
  not not_1 (not_1_out, RFID);
  and and_1 (out_5, not_1_out, or_1_out);
endmodule
