// Logisim project A4.circ as structural Verilog: 1 circuit, main circuit main
module main (
  input  a,
  input  b,
  output w,
  output out_4,
  output y,
  output z
);

  wire not_1_out, not_2_out;

  not not_1 (not_1_out, a);
  not not_2 (not_2_out, b);
  and and_1 (w, not_1_out, not_2_out);
  and and_2 (out_4, a, not_2_out);
  and and_3 (y, not_1_out, b);
  and and_4 (z, a, b);
endmodule
